# Fritzing sketch Button_LED_Externo (saved by Fritzing 0.9.9b)
circuit board: 6.88566cm x 5.36311cm
breadboards: 1

parts:
  LED1 = LED - 5mm [color="Red (633nm)" current=0.030 package="5 mm [THT]"]
  R1 = Resistor [tolerance=±5% resistance=220 power=0.25 package=THT]
  Arduino1 = Arduino Uno (Rev3)
  S1 = Pushbutton [package="[THT]"]

nets:
  N1: LED1.cathode, R1.Pin_0
  N2: LED1.anode, Arduino1.D12/MISO
  N3: R1.Pin_1, Arduino1.GND, S1.Pin_1, S1.Pin_2
  N4: Arduino1.D5_PWM, S1.Pin_3, S1.Pin_4
